# Fritzing sketch fritzing_sketch (saved by Fritzing 0.9.3b)

parts:
  Part1 = Arduino Uno (Rev3)
  USBTTL1 = USB TTL Serial Cable

nets:
  N1: Part1.D5_PWM, USBTTL1.TX
  5V: Part1.5V, USBTTL1.5V
  GND: Part1.GND, USBTTL1.GND

notes:
  USB TO TTL
  TX Output
  RX Input
